# Fritzing sketch schema (saved by Fritzing 0.9.4)

parts:
  Компонент1 = Arduino Nano (Rev3.0)
  R1 = Temperature Sensor (Thermistor) [thermistor_type=NTC package=THT]
  R2 = Resistor [tolerance=±5% resistance=10k package=THT]
  OLED_I2C1 = OLED 128x64 I2C Monochrome Display
  R3 = Rotary Potentiometer (Large) [maximum_resistance=100kΩ package=THT]

nets:
  GND: Компонент1.GND, R1.pin_0, OLED_I2C1.GND, R3.leg2
  N1: Компонент1.A5, OLED_I2C1.SCK
  N2: Компонент1.A4, OLED_I2C1.SDA
  N3: Компонент1.A1, R3.wiper
  N4: Компонент1.A0, R1.pin_1
  N5: R2.Pin_0, OLED_I2C1.VDD, R3.leg1
